// Logisim project Dan Hopkins 240 Processor Final.circ as structural Verilog: 26 circuits, main circuit CPU main
module CPU_main (
  output [15:0] Address_Read,
  output [15:0] InstrucMem,
  output [15:0] Reg1Disp,
  output [15:0] Reg2Disp,
  output [15:0] Reg3Disp
);

  wire and_1_out, clock_1_out, clock_2_out, comparator_1_eq, Control_datamemuse, Control_regfilewrite_2,
       not_1_out, not_2_out, not_3_out;
  wire [3:0] Branches_jumpto, Control_control___alsu, controlled_buffer_1_out;
  wire [4:0] ALSU_flagsout;
  wire [7:0] controlled_buffer_2_out, Relatives_jumpto;
  wire [15:0] adder_1_out, ALSU_result, bit_extender_1_out, Reg_File_readdata1, Reg_File_readdata2;

  assign controlled_buffer_1_out = InstrucMem[12] ? Branches_jumpto : 4'bz;  // Controlled_Buffer controlled_buffer_1
  not not_1 (not_1_out, InstrucMem[12]);
  assign controlled_buffer_2_out = not_1_out ? Relatives_jumpto : 8'bz;  // Controlled_Buffer controlled_buffer_2
  BRANCHES__b12___1 Branches (
    .JumpTo(Branches_jumpto), .SignIn__F0(ALSU_flagsout[0]), .ZeroIn__F1(ALSU_flagsout[1]),
    .OverflowIn__F2(ALSU_flagsout[2]), .CarryIn__F3(ALSU_flagsout[3]), .InstructionIn(InstrucMem));
  Adder #(.width(16)) adder_1 (.a(Address_Read), .b(16'h1), .out(adder_1_out));  // open: cin, cout
  Clock clock_1 (.out(clock_1_out));
  BRANCHES__b12___0 Relatives (
    .JumpTo(Relatives_jumpto), .SignIn__F0(ALSU_flagsout[0]), .ZeroIn__F1(ALSU_flagsout[1]),
    .OverflowIn__F2(ALSU_flagsout[2]), .CarryIn__F3(ALSU_flagsout[3]), .InstructionIn(InstrucMem));
  Register #(.width(16)) PC (.D(adder_1_out), .Q(Address_Read), .clk(clock_1_out));  // open: en, clr
  ROM #(.addrWidth(16), .dataWidth(16)) rom_1 (.addr(Address_Read), .data(InstrucMem));  // open: sel
  assign bit_extender_1_out = {{8{InstrucMem[7]}}, InstrucMem[7:0]};  // Bit_Extender bit_extender_1
  Register_File Reg_File (
    .ReadAddress1(InstrucMem[11:8]), .ReadAddress2(InstrucMem[11:8]), .WriteAddress(InstrucMem[11:8]),
    .WriteData(ALSU_result), .WriteEnable(Control_regfilewrite_2), .Reg1Disp(Reg1Disp), .Reg2Disp(Reg2Disp),
    .Reg3Disp(Reg3Disp), .ReadData1(Reg_File_readdata1), .ReadData2(Reg_File_readdata2));
  CONTROL Control (
    .Instruction(InstrucMem), .RegFileWrite(and_1_out), .RegFileWrite_2(Control_regfilewrite_2),
    .DataMemUse(Control_datamemuse), .Control___ALSU(Control_control___alsu));
  Comparator #(.width(16)) comparator_1 (.a(Address_Read), .b({16{1'b0}}), .eq(comparator_1_eq));  // open: gt, lt
  ALSU ALSU (
    .SourceA__first_reg(Reg_File_readdata1), .SourceB__second_reg(Reg_File_readdata2),
    .SourceC__Instr_7_0(bit_extender_1_out), .Full_Instruction_from_Memory(InstrucMem),
    .Control_Input(Control_control___alsu), .SignIn__F0(ALSU_flagsout[0]), .ZeroIn__F1(ALSU_flagsout[1]),
    .OverflowIn__F2(ALSU_flagsout[2]), .CarryIn__F3(ALSU_flagsout[3]), .CarryBlockIn__F4(ALSU_flagsout[4]),
    .FlagsOut(ALSU_flagsout), .Result(ALSU_result));
  LED F0 (.in(ALSU_flagsout[0]));
  assign ALSU_flagsout[0] = comparator_1_eq ? ~comparator_1_eq : 1'bz;  // Controlled_Inverter controlled_inverter_1
  LED F3 (.in(ALSU_flagsout[3]));
  LED F1 (.in(ALSU_flagsout[1]));
  LED F4 (.in(ALSU_flagsout[4]));
  LED F2 (.in(ALSU_flagsout[2]));
  assign ALSU_flagsout[1] = comparator_1_eq ? ~comparator_1_eq : 1'bz;  // Controlled_Inverter controlled_inverter_2
  assign ALSU_flagsout[2] = comparator_1_eq ? ~comparator_1_eq : 1'bz;  // Controlled_Inverter controlled_inverter_3
  assign ALSU_flagsout[3] = comparator_1_eq ? ~comparator_1_eq : 1'bz;  // Controlled_Inverter controlled_inverter_4
  assign ALSU_flagsout[4] = comparator_1_eq ? ~comparator_1_eq : 1'bz;  // Controlled_Inverter controlled_inverter_5
  and and_1 (and_1_out, Control_datamemuse, not_3_out);
  not not_2 (not_2_out, Control_datamemuse);
  not not_3 (not_3_out, clock_2_out);
  Clock clock_2 (.out(clock_2_out));
  RAM #(.addrWidth(4), .dataWidth(16), .bus("separate")) ram_1 (
    .addr(InstrucMem[11:8]), .din(Reg_File_readdata1), .data(ALSU_result), .str(Control_datamemuse),
    .clk(clock_2_out), .ld(not_2_out));  // open: sel, clr

  // Notes on the sheet:
  //   some way to adjust PC
  //   Instruc Mem
  //   d
  //   full instruction
  //   instruction details (low bits)
  //   WriteEnables
  //   Rd
  //   flags are set to 0 when PC = 0000
  //   RegisterWrite
  //   Result
  //   LED bar
  //   write data back to register file
  //   Data Mem
endmodule

module Register_File (
  input  [3:0] ReadAddress1,
  input  [3:0] ReadAddress2,
  input  [3:0] WriteAddress,
  input  WriteEnable,
  input  [15:0] WriteData,
  output [15:0] ReadData1,
  output [15:0] ReadData2,
  output [15:0] Reg1Disp,
  output [15:0] Reg2Disp,
  output [15:0] Reg3Disp
);

  wire and_1_out, and_2_out, and_3_out, and_4_out, and_5_out, and_6_out, and_7_out, and_8_out, and_9_out,
       and_10_out, and_11_out, and_12_out, and_13_out, and_14_out, and_15_out, and_16_out, CLK_out,
       decoder_1_out0, decoder_1_out1, decoder_1_out2, decoder_1_out3, decoder_1_out4, decoder_1_out5,
       decoder_1_out6, decoder_1_out7, decoder_1_out8, decoder_1_out9, decoder_1_out10, decoder_1_out11,
       decoder_1_out12, decoder_1_out13, decoder_1_out14, decoder_1_out15;
  wire [15:0] R0_q, R4_q, R5_q, R6_q, R7_q, R8_q, R9_q, R10_q, R11_q, R12_q, R13_q, R14_q, R15_q;

  Decoder #(.select(4), .enable("false")) decoder_1 (
    .out0(decoder_1_out0), .out1(decoder_1_out1), .out2(decoder_1_out2), .out3(decoder_1_out3),
    .out4(decoder_1_out4), .out5(decoder_1_out5), .out6(decoder_1_out6), .out7(decoder_1_out7),
    .out8(decoder_1_out8), .out9(decoder_1_out9), .out10(decoder_1_out10), .out11(decoder_1_out11),
    .out12(decoder_1_out12), .out13(decoder_1_out13), .out14(decoder_1_out14), .out15(decoder_1_out15),
    .sel(WriteAddress));
  and and_1 (and_1_out, decoder_1_out0, WriteEnable);
  and and_2 (and_2_out, decoder_1_out1, WriteEnable);
  and and_3 (and_3_out, decoder_1_out2, WriteEnable);
  and and_4 (and_4_out, decoder_1_out3, WriteEnable);
  and and_5 (and_5_out, decoder_1_out4, WriteEnable);
  and and_6 (and_6_out, decoder_1_out5, WriteEnable);
  and and_7 (and_7_out, decoder_1_out6, WriteEnable);
  and and_8 (and_8_out, decoder_1_out7, WriteEnable);
  and and_9 (and_9_out, decoder_1_out8, WriteEnable);
  and and_10 (and_10_out, decoder_1_out9, WriteEnable);
  and and_11 (and_11_out, decoder_1_out10, WriteEnable);
  and and_12 (and_12_out, decoder_1_out11, WriteEnable);
  and and_13 (and_13_out, decoder_1_out12, WriteEnable);
  and and_14 (and_14_out, decoder_1_out13, WriteEnable);
  and and_15 (and_15_out, decoder_1_out14, WriteEnable);
  and and_16 (and_16_out, decoder_1_out15, WriteEnable);
  Register #(.width(16)) R0 (.D(WriteData), .en(and_1_out), .Q(R0_q), .clk(CLK_out), .clr(1'b1));
  Clock CLK (.out(CLK_out));
  Register #(.width(16)) R1 (.D(WriteData), .en(and_2_out), .Q(Reg1Disp), .clk(CLK_out));  // open: clr
  Register #(.width(16)) R2 (.D(WriteData), .en(and_3_out), .Q(Reg2Disp), .clk(CLK_out));  // open: clr
  Register #(.width(16)) R3 (.D(WriteData), .en(and_4_out), .Q(Reg3Disp), .clk(CLK_out));  // open: clr
  Register #(.width(16)) R4 (.D(WriteData), .en(and_5_out), .Q(R4_q), .clk(CLK_out));  // open: clr
  Register #(.width(16)) R5 (.D(WriteData), .en(and_6_out), .Q(R5_q), .clk(CLK_out));  // open: clr
  Register #(.width(16)) R6 (.D(WriteData), .en(and_7_out), .Q(R6_q), .clk(CLK_out));  // open: clr
  Register #(.width(16)) R7 (.D(WriteData), .en(and_8_out), .Q(R7_q), .clk(CLK_out));  // open: clr
  Register #(.width(16)) R8 (.D(WriteData), .en(and_9_out), .Q(R8_q), .clk(CLK_out));  // open: clr
  Register #(.width(16)) R9 (.D(WriteData), .en(and_10_out), .Q(R9_q), .clk(CLK_out));  // open: clr
  Register #(.width(16)) R10 (.D(WriteData), .en(and_11_out), .Q(R10_q), .clk(CLK_out));  // open: clr
  Register #(.width(16)) R11 (.D(WriteData), .en(and_12_out), .Q(R11_q), .clk(CLK_out));  // open: clr
  Register #(.width(16)) R12 (.D(WriteData), .en(and_13_out), .Q(R12_q), .clk(CLK_out));  // open: clr
  Multiplexer #(.select(4), .width(16), .enable("false")) multiplexer_1 (
    .in0(R0_q), .in1(Reg1Disp), .in2(Reg2Disp), .in3(Reg3Disp), .in4(R4_q), .in5(R5_q), .in6(R6_q),
    .in7(R7_q), .in8(R8_q), .in9(R9_q), .in10(R10_q), .in11(R11_q), .in12(R12_q), .in13(R13_q), .in14(R14_q),
    .in15(R15_q), .out(ReadData1), .sel(ReadAddress1));
  Register #(.width(16)) R13 (.D(WriteData), .en(and_14_out), .Q(R13_q), .clk(CLK_out));  // open: clr
  Register #(.width(16)) R14 (.D(WriteData), .en(and_15_out), .Q(R14_q), .clk(CLK_out));  // open: clr
  Register #(.width(16)) R15 (.D(WriteData), .en(and_16_out), .Q(R15_q), .clk(CLK_out));  // open: clr
  Multiplexer #(.select(4), .width(16), .enable("false")) multiplexer_2 (
    .in0(R0_q), .in1(Reg1Disp), .in2(Reg2Disp), .in3(Reg3Disp), .in4(R4_q), .in5(R5_q), .in6(R6_q),
    .in7(R7_q), .in8(R8_q), .in9(R9_q), .in10(R10_q), .in11(R11_q), .in12(R12_q), .in13(R13_q), .in14(R14_q),
    .in15(R15_q), .out(ReadData2), .sel(ReadAddress2));
endmodule

module CONTROL (
  input  RegFileWrite,
  input  [15:0] Instruction,
  output [3:0] Control___ALSU,
  output RegFileWrite_2,
  output DataMemUse
);

  wire and_1_out, controlled_buffer_1_out, controlled_buffer_2_out, not_1_out;

  not not_1 (not_1_out, Instruction[15]);
  and and_1 (and_1_out, not_1_out, Instruction[14]);
  assign controlled_buffer_1_out = and_1_out ? and_1_out : 1'bz;  // Controlled_Buffer controlled_buffer_1
  assign controlled_buffer_2_out = and_1_out ? Instruction[13] : 1'bz;  // Controlled_Buffer controlled_buffer_2
  and and_2 (DataMemUse, controlled_buffer_1_out, controlled_buffer_2_out);

  assign Control___ALSU = Instruction[15:12];
  assign RegFileWrite_2 = RegFileWrite;

  // Notes on the sheet:
  //   0 = LOAD
  //   1 = STORE
  //   E = neither
endmodule

module ALSU (
  input  [3:0] Control_Input,
  input  [15:0] SourceA__first_reg,
  input  [15:0] SourceB__second_reg,
  input  [15:0] SourceC__Instr_7_0,
  input  [15:0] Full_Instruction_from_Memory,
  input  CarryBlockIn__F4,
  input  CarryIn__F3,
  input  OverflowIn__F2,
  input  ZeroIn__F1,
  input  SignIn__F0,
  output [4:0] FlagsOut,
  output [15:0] Result
);

  wire ADD_carryout__f3, ADD_overflow__f2, ADD_sign__f0, ADD_zero__f1, AND_sign__f0, AND_zero__f1,
       OR_sign__f0, OR_zero__f1, SIF_carryblockout__f4, SIF_carryout__f3, SIF_overflowout__f2,
       SIF_signout__f0, SIF_zeroout__f1, SUB_carryout__f3, SUB_overflow__f2, SUB_sign__f0, SUB_zero__f1,
       undriven, undriven_3, undriven_4, XOR_sign__f0, XOR_zero__f1;
  wire [15:0] ADD_output, AND_output, OR_output, SETHI_regout, SETLO_regout, SIF_regout, SUB_output,
       undriven_2, XOR_output;

  SIF__shifts__increments__flags__0011 SIF (
    .Full_Instruction_from_Memory(Full_Instruction_from_Memory), .SourceA__Rd(SourceA__first_reg),
    .SignIn__F0(SignIn__F0), .ZeroIn__F1(ZeroIn__F1), .OverflowIn__F2(OverflowIn__F2),
    .CarryIn__F3(CarryIn__F3), .CarryBlockIn__F4(CarryBlockIn__F4), .RegOut(SIF_regout),
    .SignOut__F0(SIF_signout__f0), .ZeroOut__F1(SIF_zeroout__f1), .OverflowOut__F2(SIF_overflowout__f2),
    .CarryOut__F3(SIF_carryout__f3), .CarryBlockOut__F4(SIF_carryblockout__f4));
  AND AND (
    .Input1(SourceA__first_reg), .Input2(SourceC__Instr_7_0), .Output(AND_output), .Sign__F0(AND_sign__f0),
    .Zero__F1(AND_zero__f1));
  OR OR (
    .Input1(SourceA__first_reg), .Input2(SourceC__Instr_7_0), .Output(OR_output), .Sign__F0(OR_sign__f0),
    .Zero__F1(OR_zero__f1));
  ADD ADD (
    .Input1(SourceA__first_reg), .Input2(SourceC__Instr_7_0), .CarryIn__F3(CarryIn__F3),
    .CarryBlock__F4(CarryBlockIn__F4), .Output(ADD_output), .Sign__F0(ADD_sign__f0), .Zero__F1(ADD_zero__f1),
    .Overflow__F2(ADD_overflow__f2), .CarryOut__F3(ADD_carryout__f3));
  SUB SUB (
    .Input1(SourceA__first_reg), .Input2(SourceC__Instr_7_0), .CarryIn__F3(CarryIn__F3),
    .CarryBlock__F4(CarryBlockIn__F4), .Output(SUB_output), .Sign__F0(SUB_sign__f0), .Zero__F1(SUB_zero__f1),
    .Overflow__F2(SUB_overflow__f2), .CarryOut__F3(SUB_carryout__f3));
  XOR XOR (
    .Input1(SourceA__first_reg), .Input2(SourceC__Instr_7_0), .Output(XOR_output), .Sign__F0(XOR_sign__f0),
    .Zero__F1(XOR_zero__f1));
  SETLO SETLO (.Instruction(SourceA__first_reg), .RegIn(SourceC__Instr_7_0), .RegOut(SETLO_regout));
  SETHI SETHI (.Instruction(SourceA__first_reg), .RegIn(SourceC__Instr_7_0), .RegOut(SETHI_regout));
  Multiplexer #(.select(4), .width(16), .enable("false")) multiplexer_1 (
    .in3(SIF_regout), .in8(AND_output), .in9(OR_output), .in10(ADD_output), .in11(SUB_output),
    .in12(undriven_2), .in13(XOR_output), .in14(SETLO_regout), .in15(SETHI_regout), .out(Result),
    .sel(Control_Input));  // open: in0, in1, in2, in4, in5, in6, in7
  LED SignOut__F0 (.in(FlagsOut[0]));
  Multiplexer #(.select(4), .enable("false")) multiplexer_2 (
    .in3(SIF_signout__f0), .in8(AND_sign__f0), .in9(OR_sign__f0), .in10(ADD_sign__f0), .in11(SUB_sign__f0),
    .in12(undriven_3), .in13(XOR_sign__f0), .in14(SignIn__F0), .in15(SignIn__F0), .out(FlagsOut[0]),
    .sel(Control_Input));  // open: in0, in1, in2, in4, in5, in6, in7
  LED ZeroOut__F1 (.in(FlagsOut[1]));
  Multiplexer #(.select(4), .enable("false")) multiplexer_3 (
    .in3(SIF_zeroout__f1), .in8(AND_zero__f1), .in9(OR_zero__f1), .in10(ADD_zero__f1), .in11(SUB_zero__f1),
    .in12(undriven), .in13(XOR_zero__f1), .in14(ZeroIn__F1), .in15(ZeroIn__F1), .out(FlagsOut[1]),
    .sel(Control_Input));  // open: in0, in1, in2, in4, in5, in6, in7
  LED OverflowOut__F2 (.in(FlagsOut[2]));
  Multiplexer #(.select(4), .enable("false")) multiplexer_4 (
    .in3(SIF_overflowout__f2), .in8(OverflowIn__F2), .in9(OverflowIn__F2), .in10(ADD_overflow__f2),
    .in11(SUB_overflow__f2), .in12(undriven_4), .in13(OverflowIn__F2), .in14(OverflowIn__F2),
    .in15(OverflowIn__F2), .out(FlagsOut[2]), .sel(Control_Input));  // open: in0, in1, in2, in4, in5, in6, in7
  LED CarryOut__F3 (.in(FlagsOut[3]));
  Multiplexer #(.select(4), .enable("false")) multiplexer_5 (
    .in3(SIF_carryout__f3), .in8(CarryIn__F3), .in9(CarryIn__F3), .in10(ADD_carryout__f3),
    .in11(SUB_carryout__f3), .in12(CarryIn__F3), .in13(CarryIn__F3), .in14(CarryIn__F3), .in15(CarryIn__F3),
    .out(FlagsOut[3]), .sel(Control_Input));  // open: in0, in1, in2, in4, in5, in6, in7
  LED CarryBlockOut__F4 (.in(FlagsOut[4]));
  Multiplexer #(.select(4), .enable("false")) multiplexer_6 (
    .in3(SIF_carryblockout__f4), .in8(CarryBlockIn__F4), .in9(CarryBlockIn__F4), .in10(CarryBlockIn__F4),
    .in11(CarryBlockIn__F4), .in12(CarryBlockIn__F4), .in13(CarryBlockIn__F4), .in14(CarryBlockIn__F4),
    .in15(CarryBlockIn__F4), .out(FlagsOut[4]), .sel(Control_Input));  // open: in0, in1, in2, in4, in5, in6, in7

  // Other names for the same wires on the sheet: c[3:0] = Control_Input

  // Notes on the sheet:
  //   MULT
endmodule

module SIF__shifts__increments__flags__0011 (
  input  CarryBlockIn__F4,
  input  SignIn__F0,
  input  ZeroIn__F1,
  input  OverflowIn__F2,
  input  CarryIn__F3,
  input  [15:0] Full_Instruction_from_Memory,
  input  [15:0] SourceA__Rd,
  output [15:0] RegOut,
  output SignOut__F0,
  output ZeroOut__F1,
  output OverflowOut__F2,
  output CarryOut__F3,
  output CarryBlockOut__F4
);

  wire [15:0] DEC_decout, INC_incout, Shifter_regout;
  wire [19:16] DEC_sign__f0, INC_sign__f0, Shifter_signout__f0;
  wire [20:16] CLRF_signout__f0, SETF_signout__f0;

  SETF SETF (
    .Instruction(Full_Instruction_from_Memory), .SignIn__F0(SignIn__F0), .ZeroIn__F1(ZeroIn__F1),
    .OverflowIn__F2(OverflowIn__F2), .CarryIn__F3(CarryIn__F3), .CarryBlockIn__F4(CarryBlockIn__F4),
    .SignOut__F0(SETF_signout__f0[16]), .ZeroOut__F1(SETF_signout__f0[17]),
    .OverflowOut__F2(SETF_signout__f0[18]), .CarryOut__F3(SETF_signout__f0[19]),
    .CarryBlockOut__F4(SETF_signout__f0[20]));
  CLRF CLRF (
    .Instruction(Full_Instruction_from_Memory), .SignIn__F0(SignIn__F0), .ZeroIn__F1(ZeroIn__F1),
    .OverflowIn__F2(OverflowIn__F2), .CarryIn__F3(CarryIn__F3), .CarryBlockIn__F4(CarryBlockIn__F4),
    .SignOut__F0(CLRF_signout__f0[16]), .ZeroOut__F1(CLRF_signout__f0[17]),
    .OverflowOut__F2(CLRF_signout__f0[18]), .CarryOut__F3(CLRF_signout__f0[19]),
    .CarryBlockOut__F4(CLRF_signout__f0[20]));
  Shifter Shifter (
    .Instruction(Full_Instruction_from_Memory), .RegIn(SourceA__Rd), .SignIn__F0(SignIn__F0),
    .ZeroIn__F1(ZeroIn__F1), .CarryIn__F3(CarryIn__F3), .CarryBlockIn__F4(CarryBlockIn__F4),
    .RegOut(Shifter_regout), .SignOut__F0(Shifter_signout__f0[16]), .ZeroOut__F1(Shifter_signout__f0[17]),
    .CarryOut__F3(Shifter_signout__f0[19]));
  INC INC (
    .Instruction(Full_Instruction_from_Memory), .RegIn(SourceA__Rd), .INCout(INC_incout),
    .Sign__F0(INC_sign__f0[16]), .Zero__F1(INC_sign__f0[17]), .Overflow__F2(INC_sign__f0[18]),
    .Carry__F3(INC_sign__f0[19]));
  DEC DEC (
    .Instruction(Full_Instruction_from_Memory), .RegIn(SourceA__Rd), .DECout(DEC_decout),
    .Sign__F0(DEC_sign__f0[16]), .Zero__F1(DEC_sign__f0[17]), .Overflow__F2(DEC_sign__f0[18]),
    .Carry__F3(DEC_sign__f0[19]));
  Multiplexer #(.select(5), .width(21), .enable("false")) multiplexer_1 (
    .in0({CarryBlockIn__F4, Shifter_signout__f0[19], OverflowIn__F2, Shifter_signout__f0[17:16], Shifter_regout}),
    .in1({CarryBlockIn__F4, Shifter_signout__f0[19], OverflowIn__F2, Shifter_signout__f0[17:16], Shifter_regout}),
    .in2({CarryBlockIn__F4, Shifter_signout__f0[19], OverflowIn__F2, Shifter_signout__f0[17:16], Shifter_regout}),
    .in3({CarryBlockIn__F4, Shifter_signout__f0[19], OverflowIn__F2, Shifter_signout__f0[17:16], Shifter_regout}),
    .in4({CarryBlockIn__F4, Shifter_signout__f0[19], OverflowIn__F2, Shifter_signout__f0[17:16], Shifter_regout}),
    .in5({CarryBlockIn__F4, Shifter_signout__f0[19], OverflowIn__F2, Shifter_signout__f0[17:16], Shifter_regout}),
    .in6({SETF_signout__f0, SourceA__Rd}), .in8({CarryBlockIn__F4, INC_sign__f0, INC_incout}),
    .in9({CarryBlockIn__F4, INC_sign__f0, INC_incout}), .in10({CarryBlockIn__F4, INC_sign__f0, INC_incout}),
    .in11({CarryBlockIn__F4, INC_sign__f0, INC_incout}), .in12({CarryBlockIn__F4, DEC_sign__f0, DEC_decout}),
    .in13({CarryBlockIn__F4, DEC_sign__f0, DEC_decout}), .in14({CarryBlockIn__F4, DEC_sign__f0, DEC_decout}),
    .in15({CarryBlockIn__F4, DEC_sign__f0, DEC_decout}),
    .in16({CarryBlockIn__F4, Shifter_signout__f0[19], OverflowIn__F2, Shifter_signout__f0[17:16], Shifter_regout}),
    .in17({CarryBlockIn__F4, Shifter_signout__f0[19], OverflowIn__F2, Shifter_signout__f0[17:16], Shifter_regout}),
    .in18({CarryBlockIn__F4, Shifter_signout__f0[19], OverflowIn__F2, Shifter_signout__f0[17:16], Shifter_regout}),
    .in19({CarryBlockIn__F4, Shifter_signout__f0[19], OverflowIn__F2, Shifter_signout__f0[17:16], Shifter_regout}),
    .in20({CarryBlockIn__F4, Shifter_signout__f0[19], OverflowIn__F2, Shifter_signout__f0[17:16], Shifter_regout}),
    .in21({CarryBlockIn__F4, Shifter_signout__f0[19], OverflowIn__F2, Shifter_signout__f0[17:16], Shifter_regout}),
    .in22({CLRF_signout__f0, SourceA__Rd}), .in24({CarryBlockIn__F4, INC_sign__f0, INC_incout}),
    .in25({CarryBlockIn__F4, INC_sign__f0, INC_incout}), .in26({CarryBlockIn__F4, INC_sign__f0, INC_incout}),
    .in27({CarryBlockIn__F4, INC_sign__f0, INC_incout}), .in28({CarryBlockIn__F4, DEC_sign__f0, DEC_decout}),
    .in29({CarryBlockIn__F4, DEC_sign__f0, DEC_decout}), .in30({CarryBlockIn__F4, DEC_sign__f0, DEC_decout}),
    .in31({CarryBlockIn__F4, DEC_sign__f0, DEC_decout}),
    .out({CarryBlockOut__F4, CarryOut__F3, OverflowOut__F2, ZeroOut__F1, SignOut__F0, RegOut}),
    .sel({Full_Instruction_from_Memory[11], Full_Instruction_from_Memory[7:4]}));  // open: in7, in23

  // Other names for the same wires on the sheet: S[15:0] = SourceA__Rd; O = OverflowIn__F2; B = CarryBlockIn__F4
endmodule

module Data_Memory (
  input  WriteEnable,
  input  [15:0] Address,
  input  [15:0] WriteData,
  output [15:0] ReadData
);

  wire CLK_out, not_1_out;

  Clock CLK (.out(CLK_out));
  RAM #(.addrWidth(16), .dataWidth(16), .bus("separate")) ram_1 (
    .addr(Address), .din(WriteData), .data(ReadData), .str(WriteEnable), .clk(CLK_out), .ld(not_1_out));  // open: sel, clr
  not not_1 (not_1_out, WriteEnable);
endmodule

module BRANCHES__b12___1 (
  input  CarryIn__F3,
  input  OverflowIn__F2,
  input  ZeroIn__F1,
  input  SignIn__F0,
  input  [15:0] InstructionIn,
  output [3:0] JumpTo
);

  wire and_1_out, and_2_out, and_3_out, and_4_out, and_5_out, and_6_out, and_7_out, and_8_out, and_9_out,
       and_10_out, and_11_out, and_12_out, and_13_out, and_14_out, BC_out, BG_out, BGE_out, BL_out, BLE_out,
       BNC_out, BNS_out, BNV_out, BNZ_out, BR_out, BS_out, BUG_out, BULE_out, BV_out, BZ_out, nor_1_out,
       nor_2_out, not_1_out, not_2_out, not_3_out, not_4_out, not_5_out, not_6_out, not_7_out, not_8_out,
       not_9_out, not_10_out, not_11_out, not_12_out, not_13_out, not_14_out, not_15_out, not_16_out,
       not_17_out, not_18_out, not_19_out, not_20_out, not_21_out, not_22_out, not_23_out, not_24_out,
       not_25_out, not_26_out, not_27_out, not_28_out, not_29_out, not_30_out, not_31_out, not_32_out,
       not_33_out, not_34_out, not_35_out, not_36_out, or_1_out, or_2_out, or_3_out, xor_1_out, xor_2_out,
       xor_3_out, xor_4_out;

  not not_1 (not_1_out, InstructionIn[8]);
  not not_2 (not_2_out, InstructionIn[9]);
  and BR (BR_out, not_1_out, not_2_out, not_3_out, not_4_out);
  not not_3 (not_3_out, InstructionIn[10]);
  not not_4 (not_4_out, InstructionIn[11]);
  not not_5 (not_5_out, InstructionIn[8]);
  and BL (BL_out, not_5_out, InstructionIn[9], not_6_out, not_7_out);
  not not_6 (not_6_out, InstructionIn[10]);
  not not_7 (not_7_out, InstructionIn[11]);
  and BGE (BGE_out, InstructionIn[8], InstructionIn[9], not_8_out, not_9_out);
  not not_8 (not_8_out, InstructionIn[10]);
  not not_9 (not_9_out, InstructionIn[11]);
  not not_10 (not_10_out, InstructionIn[8]);
  not not_11 (not_11_out, InstructionIn[9]);
  and BLE (BLE_out, not_10_out, not_11_out, InstructionIn[10], not_12_out);
  not not_12 (not_12_out, InstructionIn[11]);
  not not_13 (not_13_out, InstructionIn[9]);
  and BG (BG_out, InstructionIn[8], not_13_out, InstructionIn[10], not_14_out);
  not not_14 (not_14_out, InstructionIn[11]);
  not not_15 (not_15_out, InstructionIn[8]);
  and BULE (BULE_out, not_15_out, InstructionIn[9], InstructionIn[10], not_16_out);
  not not_16 (not_16_out, InstructionIn[11]);
  and BUG (BUG_out, InstructionIn[8], InstructionIn[9], InstructionIn[10], not_17_out);
  not not_17 (not_17_out, InstructionIn[11]);
  not not_18 (not_18_out, InstructionIn[8]);
  not not_19 (not_19_out, InstructionIn[9]);
  and BZ (BZ_out, not_18_out, not_19_out, not_20_out, InstructionIn[11]);
  not not_20 (not_20_out, InstructionIn[10]);
  not not_21 (not_21_out, InstructionIn[9]);
  and BNZ (BNZ_out, InstructionIn[8], not_21_out, not_22_out, InstructionIn[11]);
  not not_22 (not_22_out, InstructionIn[10]);
  not not_23 (not_23_out, InstructionIn[8]);
  and BC (BC_out, not_23_out, InstructionIn[9], not_24_out, InstructionIn[11]);
  not not_24 (not_24_out, InstructionIn[10]);
  and BNC (BNC_out, InstructionIn[8], InstructionIn[9], not_25_out, InstructionIn[11]);
  not not_25 (not_25_out, InstructionIn[10]);
  not not_26 (not_26_out, InstructionIn[8]);
  not not_27 (not_27_out, InstructionIn[9]);
  and BS (BS_out, not_26_out, not_27_out, InstructionIn[10], InstructionIn[11]);
  not not_28 (not_28_out, InstructionIn[9]);
  and BNS (BNS_out, InstructionIn[8], not_28_out, InstructionIn[10], InstructionIn[11]);
  not not_29 (not_29_out, InstructionIn[8]);
  and BV (BV_out, not_29_out, InstructionIn[9], InstructionIn[10], InstructionIn[11]);
  and BNV (BNV_out, InstructionIn[8], InstructionIn[9], InstructionIn[10], InstructionIn[11]);
  not not_30 (not_30_out, SignIn__F0);
  not not_31 (not_31_out, ZeroIn__F1);
  and and_1 (and_1_out, SignIn__F0, BS_out);
  and and_2 (and_2_out, not_30_out, BNS_out);
  and and_3 (and_3_out, ZeroIn__F1, BZ_out);
  and and_4 (and_4_out, not_31_out, BNZ_out);
  not not_32 (not_32_out, OverflowIn__F2);
  xor xor_1 (xor_1_out, OverflowIn__F2, SignIn__F0);
  xor xor_2 (xor_2_out, OverflowIn__F2, SignIn__F0);
  xor xor_3 (xor_3_out, OverflowIn__F2, SignIn__F0);
  xor xor_4 (xor_4_out, OverflowIn__F2, SignIn__F0);
  not not_33 (not_33_out, CarryIn__F3);
  and and_5 (and_5_out, OverflowIn__F2, BV_out);
  and and_6 (and_6_out, not_32_out, BNV_out);
  and and_7 (and_7_out, xor_1_out, BL_out);
  not not_34 (not_34_out, xor_2_out);
  or or_1 (or_1_out, xor_3_out, ZeroIn__F1);
  nor nor_1 (nor_1_out, xor_4_out, ZeroIn__F1);
  not not_35 (not_35_out, CarryIn__F3);
  or or_2 (or_2_out, not_35_out, ZeroIn__F1);
  not not_36 (not_36_out, CarryIn__F3);
  and and_8 (and_8_out, CarryIn__F3, BC_out);
  and and_9 (and_9_out, not_33_out, BNC_out);
  and and_10 (and_10_out, not_34_out, BGE_out);
  and and_11 (and_11_out, or_1_out, BLE_out);
  and and_12 (and_12_out, nor_1_out, BG_out);
  and and_13 (and_13_out, or_2_out, BULE_out);
  nor nor_2 (nor_2_out, not_36_out, ZeroIn__F1);
  and and_14 (and_14_out, nor_2_out, BUG_out);
  assign JumpTo = or_3_out ? InstructionIn[3:0] : 4'bz;  // Controlled_Buffer controlled_buffer_1
  or or_3 (or_3_out, BR_out, and_7_out, and_10_out, and_11_out, and_12_out, and_13_out, and_14_out, and_3_out, and_4_out, and_8_out, and_9_out, and_1_out, and_2_out, and_5_out, and_6_out);

  // Notes on the sheet:
  //   if b15:12 = 000, then its a branch
  //   if any of these and gates produce 1, then we want to return b3:0
endmodule

module BRANCHES__b12___0 (
  input  CarryIn__F3,
  input  OverflowIn__F2,
  input  ZeroIn__F1,
  input  SignIn__F0,
  input  [15:0] InstructionIn,
  output [7:0] JumpTo
);

  wire and_1_out, and_2_out, and_3_out, and_4_out, and_5_out, and_6_out, and_7_out, and_8_out, and_9_out,
       and_10_out, and_11_out, and_12_out, and_13_out, and_14_out, BCR_out, BGER_out, BGR_out, BLER_out,
       BLR_out, BNCR_out, BNSR_out, BNVR_out, BNZR_out, BRR_out, BSR_out, BUGR_out, BULER_out, BVR_out,
       BZR_out, nor_1_out, nor_2_out, not_1_out, not_2_out, not_3_out, not_4_out, not_5_out, not_6_out,
       not_7_out, not_8_out, not_9_out, not_10_out, not_11_out, not_12_out, not_13_out, not_14_out,
       not_15_out, not_16_out, not_17_out, not_18_out, not_19_out, not_20_out, not_21_out, not_22_out,
       not_23_out, not_24_out, not_25_out, not_26_out, not_27_out, not_28_out, not_29_out, not_30_out,
       not_31_out, not_32_out, not_33_out, not_34_out, not_35_out, not_36_out, or_1_out, or_2_out, or_3_out,
       xor_1_out, xor_2_out, xor_3_out, xor_4_out;

  not not_1 (not_1_out, InstructionIn[8]);
  not not_2 (not_2_out, InstructionIn[9]);
  and BRR (BRR_out, not_1_out, not_2_out, not_3_out, not_4_out);
  not not_3 (not_3_out, InstructionIn[10]);
  not not_4 (not_4_out, InstructionIn[11]);
  not not_5 (not_5_out, InstructionIn[8]);
  and BLR (BLR_out, not_5_out, InstructionIn[9], not_6_out, not_7_out);
  not not_6 (not_6_out, InstructionIn[10]);
  not not_7 (not_7_out, InstructionIn[11]);
  and BGER (BGER_out, InstructionIn[8], InstructionIn[9], not_8_out, not_9_out);
  not not_8 (not_8_out, InstructionIn[10]);
  not not_9 (not_9_out, InstructionIn[11]);
  not not_10 (not_10_out, InstructionIn[8]);
  not not_11 (not_11_out, InstructionIn[9]);
  and BLER (BLER_out, not_10_out, not_11_out, InstructionIn[10], not_12_out);
  not not_12 (not_12_out, InstructionIn[11]);
  not not_13 (not_13_out, InstructionIn[9]);
  and BGR (BGR_out, InstructionIn[8], not_13_out, InstructionIn[10], not_14_out);
  not not_14 (not_14_out, InstructionIn[11]);
  not not_15 (not_15_out, InstructionIn[8]);
  and BULER (BULER_out, not_15_out, InstructionIn[9], InstructionIn[10], not_16_out);
  not not_16 (not_16_out, InstructionIn[11]);
  and BUGR (BUGR_out, InstructionIn[8], InstructionIn[9], InstructionIn[10], not_17_out);
  not not_17 (not_17_out, InstructionIn[11]);
  not not_18 (not_18_out, InstructionIn[8]);
  not not_19 (not_19_out, InstructionIn[9]);
  and BZR (BZR_out, not_18_out, not_19_out, not_20_out, InstructionIn[11]);
  not not_20 (not_20_out, InstructionIn[10]);
  not not_21 (not_21_out, InstructionIn[9]);
  and BNZR (BNZR_out, InstructionIn[8], not_21_out, not_22_out, InstructionIn[11]);
  not not_22 (not_22_out, InstructionIn[10]);
  not not_23 (not_23_out, InstructionIn[8]);
  and BCR (BCR_out, not_23_out, InstructionIn[9], not_24_out, InstructionIn[11]);
  not not_24 (not_24_out, InstructionIn[10]);
  and BNCR (BNCR_out, InstructionIn[8], InstructionIn[9], not_25_out, InstructionIn[11]);
  not not_25 (not_25_out, InstructionIn[10]);
  not not_26 (not_26_out, InstructionIn[8]);
  not not_27 (not_27_out, InstructionIn[9]);
  and BSR (BSR_out, not_26_out, not_27_out, InstructionIn[10], InstructionIn[11]);
  not not_28 (not_28_out, InstructionIn[9]);
  and BNSR (BNSR_out, InstructionIn[8], not_28_out, InstructionIn[10], InstructionIn[11]);
  not not_29 (not_29_out, InstructionIn[8]);
  and BVR (BVR_out, not_29_out, InstructionIn[9], InstructionIn[10], InstructionIn[11]);
  and BNVR (BNVR_out, InstructionIn[8], InstructionIn[9], InstructionIn[10], InstructionIn[11]);
  not not_30 (not_30_out, SignIn__F0);
  not not_31 (not_31_out, ZeroIn__F1);
  and and_1 (and_1_out, SignIn__F0, BSR_out);
  and and_2 (and_2_out, not_30_out, BNSR_out);
  and and_3 (and_3_out, ZeroIn__F1, BZR_out);
  and and_4 (and_4_out, not_31_out, BNZR_out);
  not not_32 (not_32_out, OverflowIn__F2);
  xor xor_1 (xor_1_out, OverflowIn__F2, SignIn__F0);
  xor xor_2 (xor_2_out, OverflowIn__F2, SignIn__F0);
  xor xor_3 (xor_3_out, OverflowIn__F2, SignIn__F0);
  xor xor_4 (xor_4_out, OverflowIn__F2, SignIn__F0);
  not not_33 (not_33_out, CarryIn__F3);
  and and_5 (and_5_out, OverflowIn__F2, BVR_out);
  and and_6 (and_6_out, not_32_out, BNVR_out);
  and and_7 (and_7_out, xor_1_out, BLR_out);
  not not_34 (not_34_out, xor_2_out);
  or or_1 (or_1_out, xor_3_out, ZeroIn__F1);
  nor nor_1 (nor_1_out, xor_4_out, ZeroIn__F1);
  not not_35 (not_35_out, CarryIn__F3);
  or or_2 (or_2_out, not_35_out, ZeroIn__F1);
  not not_36 (not_36_out, CarryIn__F3);
  and and_8 (and_8_out, CarryIn__F3, BCR_out);
  and and_9 (and_9_out, not_33_out, BNCR_out);
  and and_10 (and_10_out, not_34_out, BGER_out);
  and and_11 (and_11_out, or_1_out, BLER_out);
  and and_12 (and_12_out, nor_1_out, BGR_out);
  and and_13 (and_13_out, or_2_out, BULER_out);
  nor nor_2 (nor_2_out, not_36_out, ZeroIn__F1);
  and and_14 (and_14_out, nor_2_out, BUGR_out);
  assign JumpTo = or_3_out ? InstructionIn[7:0] : 8'bz;  // Controlled_Buffer controlled_buffer_1
  or or_3 (or_3_out, BRR_out, and_7_out, and_10_out, and_11_out, and_12_out, and_13_out, and_14_out, and_3_out, and_4_out, and_8_out, and_9_out, and_1_out, and_2_out, and_5_out, and_6_out);

  // Notes on the sheet:
  //   if b15:12 = 000, then its a branch
  //   if any of these and gates produce 1, then we want to return b3:0
endmodule

module SETLO (
  input  [15:0] Instruction,
  input  [15:0] RegIn,
  output [15:0] RegOut
);


  assign RegOut = {RegIn[15:8], Instruction[7:0]};
endmodule

module SETHI (
  input  [15:0] Instruction,
  input  [15:0] RegIn,
  output [15:0] RegOut
);


  assign RegOut = {Instruction[7:0], RegIn[7:0]};
endmodule

module AND (
  input  [15:0] Input1,
  input  [15:0] Input2,
  output [15:0] Output,
  output Sign__F0,
  output Zero__F1
);

  assign Output = Input1 & Input2;  // AND_Gate and_1, 16 bits wide
  Comparator #(.width(16), .mode("unsigned")) comparator_1 (.a(Output), .b({16{1'b0}}), .eq(Zero__F1));  // open: gt, lt

  assign Sign__F0 = Output[15];
endmodule

module OR (
  input  [15:0] Input1,
  input  [15:0] Input2,
  output [15:0] Output,
  output Sign__F0,
  output Zero__F1
);

  assign Output = Input1 | Input2;  // OR_Gate or_1, 16 bits wide
  Comparator #(.width(16), .mode("unsigned")) comparator_1 (.a(Output), .b({16{1'b0}}), .eq(Zero__F1));  // open: gt, lt

  assign Sign__F0 = Output[15];
endmodule

module ADD (
  input  CarryIn__F3,
  input  CarryBlock__F4,
  input  [15:0] Input1,
  input  [15:0] Input2,
  output [15:0] Output,
  output Sign__F0,
  output Zero__F1,
  output Overflow__F2,
  output CarryOut__F3
);

  wire and_1_out, comparator_1_eq, comparator_3_eq, not_1_out, not_2_out;

  and and_1 (and_1_out, CarryIn__F3, not_1_out);
  Adder #(.width(16)) adder_1 (.a(Input1), .b(Input2), .out(Output), .cin(and_1_out), .cout(CarryOut__F3));
  Comparator #(.width(1)) comparator_1 (.a(Input2[15]), .b(Input1[15]), .eq(comparator_1_eq));  // open: gt, lt
  not not_1 (not_1_out, CarryBlock__F4);
  Comparator #(.width(16), .mode("unsigned")) comparator_2 (.a(Output), .b({16{1'b0}}), .eq(Zero__F1));  // open: gt, lt
  Comparator #(.width(1)) comparator_3 (.a(Output[15]), .b(Input1[15]), .eq(comparator_3_eq));  // open: gt, lt
  not not_2 (not_2_out, comparator_3_eq);
  and and_2 (Overflow__F2, comparator_1_eq, not_2_out);

  assign Sign__F0 = Output[15];

  // Other names for the same wires on the sheet: _3 = CarryOut__F3

  // Notes on the sheet:
  //   If b15 of input 1 and 2 are the same and it is different than b15 of output, overflow = 1
endmodule

module SUB (
  input  CarryIn__F3,
  input  CarryBlock__F4,
  input  [15:0] Input1,
  input  [15:0] Input2,
  output [15:0] Output,
  output Sign__F0,
  output Zero__F1,
  output Overflow__F2,
  output CarryOut__F3
);

  wire and_1_out, comparator_1_eq, comparator_3_eq, not_1_out, not_2_out, not_3_out;

  and and_1 (and_1_out, CarryIn__F3, not_2_out);
  not not_1 (not_1_out, and_1_out);
  Subtractor #(.width(16)) subtractor_1 (.a(Input1), .b(Input2), .out(Output), .bin(not_1_out), .bout(CarryOut__F3));
  Comparator #(.width(1)) comparator_1 (.a(Input2[15]), .b(Input1[15]), .eq(comparator_1_eq));  // open: gt, lt
  not not_2 (not_2_out, CarryBlock__F4);
  Comparator #(.width(16), .mode("unsigned")) comparator_2 (.a(Output), .b({16{1'b0}}), .eq(Zero__F1));  // open: gt, lt
  Comparator #(.width(1)) comparator_3 (.a(Output[15]), .b(Input1[15]), .eq(comparator_3_eq));  // open: gt, lt
  not not_3 (not_3_out, comparator_3_eq);
  and and_2 (Overflow__F2, comparator_1_eq, not_3_out);

  assign Sign__F0 = Output[15];

  // Other names for the same wires on the sheet: _3 = CarryOut__F3
endmodule

module MULT__nd (
  input  in_1,
  input  [15:0] Input1,
  input  [15:0] Input2,
  input  [3:0] in_4,
  input  [3:0] in_5,
  input  [3:0] in_6,
  output Sign__F0,
  output [15:0] out_8,
  output Zero__F1,
  output Overflow__F2,
  output [3:0] out_11,
  output [3:0] out_12
);

  Multiplier #(.width(16)) multiplier_1 (.a(Input1), .b(Input2), .out(out_8));  // open: cin, cout
  Multiplier #(.width(4)) multiplier_2 (.a(in_5), .b(in_6), .out(out_11), .cin(in_4), .cout(out_12));

  // Notes on the sheet:
  //   The multiplication operation computes the product of Ra and Rb, treated as signed integer quantities. It places the low-order 16 bits in Rd and the high-order 16 bits in the temporary register Rt.
  //   Modifies the zero, sign, and overflow flags (zero and sign are based on all 32 bits of the result; the overflow flag is true if and only if simply sign extending the lower 16 bits would not produce the full 32 bit result)
endmodule

module XOR (
  input  [15:0] Input1,
  input  [15:0] Input2,
  output [15:0] Output,
  output Sign__F0,
  output Zero__F1
);

  assign Output = Input1 ^ Input2;  // XOR_Gate xor_1, 16 bits wide
  Comparator #(.width(16), .mode("unsigned")) comparator_1 (.a(Output), .b({16{1'b0}}), .eq(Zero__F1));  // open: gt, lt

  assign Sign__F0 = Output[15];
endmodule

module Shifter (
  input  [15:0] Instruction,
  input  [15:0] RegIn,
  input  CarryIn__F3,
  input  CarryBlockIn__F4,
  input  SignIn__F0,
  input  ZeroIn__F1,
  output [15:0] RegOut,
  output SignOut__F0,
  output ZeroOut__F1,
  output CarryOut__F3
);

  wire LSL8_sign__f0, LSL8_zero__f1, LSL_carryout__f3, LSR8_sign__f0, LSR8_zero__f1, LSR_carryout__f3;
  wire [15:0] LSL8_regout, LSL_regout, LSR8_regout, LSR_regout;

  LSL LSL (
    .RegIn(RegIn), .CarryIn__F3(CarryIn__F3), .CarryBlock__F4(CarryBlockIn__F4), .RegOut(LSL_regout),
    .CarryOut__F3(LSL_carryout__f3));
  LSR LSR (
    .RegIn(RegIn), .CarryIn__F3(CarryIn__F3), .CarryBlock__F4(CarryBlockIn__F4), .RegOut(LSR_regout),
    .CarryOut__F3(LSR_carryout__f3));
  LSL8 LSL8 (.RegIn(RegIn), .RegOut(LSL8_regout), .Sign__F0(LSL8_sign__f0), .Zero__F1(LSL8_zero__f1));
  LSR8 LSR8 (.RegIn(RegIn), .RegOut(LSR8_regout), .Sign__F0(LSR8_sign__f0), .Zero__F1(LSR8_zero__f1));
  Multiplexer #(.select(4), .width(16), .enable("false")) multiplexer_1 (
    .in0(LSL_regout), .in1(LSR_regout), .in2(LSL8_regout), .in3(LSR8_regout), .out(RegOut),
    .sel(Instruction[7:4]));  // open: in4, in5, in6, in7, in8, in9, in10, in11, in12, in13, in14, in15
  Multiplexer #(.select(4), .enable("false")) multiplexer_2 (
    .in0(SignIn__F0), .in1(ZeroIn__F1), .in2(LSL8_sign__f0), .in3(LSR8_sign__f0), .out(SignOut__F0),
    .sel(Instruction[7:4]));  // open: in4, in5, in6, in7, in8, in9, in10, in11, in12, in13, in14, in15
  Multiplexer #(.select(4), .enable("false")) multiplexer_3 (
    .in0(SignIn__F0), .in1(ZeroIn__F1), .in2(LSL8_zero__f1), .in3(LSR8_zero__f1), .out(ZeroOut__F1),
    .sel(Instruction[7:4]));  // open: in4, in5, in6, in7, in8, in9, in10, in11, in12, in13, in14, in15
  Multiplexer #(.select(4), .enable("false")) multiplexer_4 (
    .in0(LSL_carryout__f3), .in1(LSR_carryout__f3), .in2(CarryIn__F3), .in3(CarryBlockIn__F4),
    .out(CarryOut__F3), .sel(Instruction[7:4]));  // open: in4, in5, in6, in7, in8, in9, in10, in11, in12, in13, in14, in15

  // Other names for the same wires on the sheet: f[3:0] = Instruction[7:4]
endmodule

module LSL (
  input  CarryIn__F3,
  input  CarryBlock__F4,
  input  [15:0] RegIn,
  output [15:0] RegOut,
  output CarryOut__F3
);

  wire not_1_out;

  not not_1 (not_1_out, CarryBlock__F4);
  and and_1 (RegOut[0], CarryIn__F3, not_1_out);

  assign CarryOut__F3 = RegIn[15];
  assign RegOut[15:1] = RegIn[14:0];
endmodule

module LSR (
  input  [15:0] RegIn,
  input  CarryBlock__F4,
  input  CarryIn__F3,
  output [15:0] RegOut,
  output CarryOut__F3
);

  wire not_1_out;

  and and_1 (RegOut[15], CarryIn__F3, not_1_out);
  not not_1 (not_1_out, CarryBlock__F4);

  assign CarryOut__F3 = RegIn[0];
  assign RegOut[14:0] = RegIn[15:1];
endmodule

module LSL8 (
  input  [15:0] RegIn,
  output [15:0] RegOut,
  output Sign__F0,
  output Zero__F1
);

  Comparator #(.width(16), .mode("unsigned")) comparator_1 (
    .a({RegIn[7:0], {8{1'b0}}}), .b({16{1'b0}}), .eq(Zero__F1));  // open: gt, lt

  assign RegOut = {RegIn[7:0], {8{1'b0}}};
  assign Sign__F0 = RegIn[7];
endmodule

module LSR8 (
  input  [15:0] RegIn,
  output [15:0] RegOut,
  output Sign__F0,
  output Zero__F1
);

  Comparator #(.width(16), .mode("unsigned")) comparator_1 (
    .a({{8{1'b0}}, RegIn[15:8]}), .b({16{1'b0}}), .eq(Zero__F1));  // open: gt, lt

  assign RegOut = {{8{1'b0}}, RegIn[15:8]};
  assign Sign__F0 = 1'b0;
endmodule

module SETF (
  input  SignIn__F0,
  input  ZeroIn__F1,
  input  OverflowIn__F2,
  input  CarryIn__F3,
  input  CarryBlockIn__F4,
  input  [15:0] Instruction,
  output SignOut__F0,
  output ZeroOut__F1,
  output OverflowOut__F2,
  output CarryOut__F3,
  output CarryBlockOut__F4
);

  or or_1 (SignOut__F0, SignIn__F0, Instruction[0]);
  or or_2 (ZeroOut__F1, ZeroIn__F1, Instruction[1]);
  or or_3 (OverflowOut__F2, OverflowIn__F2, Instruction[2]);
  or or_4 (CarryOut__F3, CarryIn__F3, Instruction[3]);
  or or_5 (CarryBlockOut__F4, CarryBlockIn__F4, Instruction[8]);

  // Notes on the sheet:
  //   F is F or v: set flags for which v is true
endmodule

module CLRF (
  input  SignIn__F0,
  input  ZeroIn__F1,
  input  OverflowIn__F2,
  input  CarryIn__F3,
  input  CarryBlockIn__F4,
  input  [15:0] Instruction,
  output SignOut__F0,
  output ZeroOut__F1,
  output OverflowOut__F2,
  output CarryOut__F3,
  output CarryBlockOut__F4
);

  wire not_1_out, not_2_out, not_3_out, not_4_out, not_5_out;

  not not_1 (not_1_out, SignIn__F0);
  not not_2 (not_2_out, ZeroIn__F1);
  not not_3 (not_3_out, OverflowIn__F2);
  not not_4 (not_4_out, CarryIn__F3);
  not not_5 (not_5_out, CarryBlockIn__F4);
  and and_1 (SignOut__F0, not_1_out, Instruction[0]);
  and and_2 (ZeroOut__F1, not_2_out, Instruction[1]);
  and and_3 (OverflowOut__F2, not_3_out, Instruction[2]);
  and and_4 (CarryOut__F3, not_4_out, Instruction[3]);
  and and_5 (CarryBlockOut__F4, not_5_out, Instruction[8]);

  // Notes on the sheet:
  //   F is F and v': Clear flags for which v is true
endmodule

module INC (
  input  [15:0] Instruction,
  input  [15:0] RegIn,
  output [15:0] INCout,
  output Sign__F0,
  output Zero__F1,
  output Overflow__F2,
  output Carry__F3
);

  wire [5:0] adder_1_out;
  wire [15:0] bit_extender_1_out;

  Adder #(.width(6)) adder_1 (.a(6'b000001), .b(Instruction[5:0]), .out(adder_1_out), .cin(1'b0));  // open: cout
  assign bit_extender_1_out = {{10{1'b0}}, adder_1_out};  // Bit_Extender bit_extender_1
  Comparator #(.width(16), .mode("unsigned")) comparator_1 (.a(RegIn), .b(INCout), .gt(Overflow__F2));  // open: eq, lt
  Adder #(.width(16)) adder_2 (.a(bit_extender_1_out), .b(RegIn), .out(INCout), .cout(Carry__F3));  // open: cin
  Comparator #(.width(16), .mode("unsigned")) comparator_2 (.a(INCout), .b({16{1'b0}}), .eq(Zero__F1));  // open: gt, lt

  assign Sign__F0 = INCout[15];

  // Other names for the same wires on the sheet: c = Carry__F3
endmodule

module DEC (
  input  [15:0] Instruction,
  input  [15:0] RegIn,
  output [15:0] DECout,
  output Sign__F0,
  output Zero__F1,
  output Overflow__F2,
  output Carry__F3
);

  wire [5:0] adder_1_out;
  wire [15:0] bit_extender_1_out;

  Adder #(.width(6)) adder_1 (.a(6'b000001), .b(Instruction[5:0]), .out(adder_1_out), .cin(1'b0));  // open: cout
  assign bit_extender_1_out = {{10{1'b0}}, adder_1_out};  // Bit_Extender bit_extender_1
  Comparator #(.width(16), .mode("unsigned")) comparator_1 (.a(RegIn), .b(DECout), .lt(Overflow__F2));  // open: gt, eq
  Subtractor #(.width(16)) subtractor_1 (
    .a(RegIn), .b(bit_extender_1_out), .out(DECout), .bout(Carry__F3));  // open: bin
  Comparator #(.width(16), .mode("unsigned")) comparator_2 (.a(DECout), .b({16{1'b0}}), .eq(Zero__F1));  // open: gt, lt

  assign Sign__F0 = DECout[15];

  // Other names for the same wires on the sheet: c = Carry__F3
endmodule

module Centigrade_to_Fahrenheit (
);


  // Notes on the sheet:
  //   FOR LAB 5:
  //   R1 = C
  //   R2 will be F
  //   FOR LAB 6:
  //   R2 = (R1 * 2) + 30
  //   MULT(R1, R2, 2)      // R1 = C; C*2; R1 = C*2
  //   ADD(R2, R1, 30)     // R1 = C*2; R1 + 30 = (C * 2) + 30 = F; R2 = F
  //   MULT(R2, R1, 2)     // Multiply initial centigrade value by 2, store in R2
  //   STORE(R3, 0, R1)       // STORE result into another memory location R3
  //   F = (C * 2) + 30 // Write HERA to do this assuming C is in R1, F ends up in R2
  //   LOAD(R1, 0, R3)       // LOAD value for centigrade from fixed memory location in R3
  //   ADD(R1, R2, 30)      // Add 30 to the double centigrade value in R2, store in R1
endmodule
